# Fritzing sketch Bill (saved by Fritzing 0.7.11b)
breadboards: 1
stripboards: 4

parts:
  Ri = Resistor [tolerance=±5% resistance=220 package=THT]
  R1l = Resistor [tolerance=±5% resistance=220 package=THT]
  R2l = Resistor [tolerance=±5% resistance=220 package=THT]
  RB = Resistor [tolerance=±5% resistance=220 package=THT]
  i1 = LED - 3mm [color="Red (633nm)" package="3 mm [THT]"]
  i2 = LED - 3mm [color="Red (633nm)" package="3 mm [THT]"]
  i3 = LED - 3mm [color="Red (633nm)" package="3 mm [THT]"]
  1l2 = LED - 3mm [color="Red (633nm)" package="3 mm [THT]"]
  1l4 = LED - 3mm [color="Red (633nm)" package="3 mm [THT]"]
  1l3 = LED - 3mm [color="Red (633nm)" package="3 mm [THT]"]
  2l3 = LED - 3mm [color="Red (633nm)" package="3 mm [THT]"]
  2l4 = LED - 3mm [color="Red (633nm)" package="3 mm [THT]"]
  2l5 = LED - 3mm [color="Red (633nm)" package="3 mm [THT]"]
  2l6 = LED - 3mm [color="Red (633nm)" package="3 mm [THT]"]
  1l1 = LED - 3mm [color="Red (633nm)" package="3 mm [THT]"]
  B1 = LED - 3mm [color="Red (633nm)" package="3 mm [THT]"]
  B4 = LED - 3mm [color="Red (633nm)" package="3 mm [THT]"]
  B3 = LED - 3mm [color="Red (633nm)" package="3 mm [THT]"]
  B7 = LED - 3mm [color="Red (633nm)" package="3 mm [THT]"]
  B8 = LED - 3mm [color="Red (633nm)" package="3 mm [THT]"]
  B9 = LED - 3mm [color="Red (633nm)" package="3 mm [THT]"]
  B10 = LED - 3mm [color="Red (633nm)" package="3 mm [THT]"]
  B5 = LED - 3mm [color="Red (633nm)" package="3 mm [THT]"]
  B6 = LED - 3mm [color="Red (633nm)" package="3 mm [THT]"]
  B2 = LED - 3mm [color="Red (633nm)" package="3 mm [THT]"]
  Arduino = Arduino
  Reset = Pushbutton [package="[THT]"]
  Mode = Pushbutton [package="[THT]"]
  2l2 = LED - 3mm [color="Red (633nm)" package="3 mm [THT]"]
  2l1 = LED - 3mm [color="Red (633nm)" package="3 mm [THT]"]
  1l5 = LED - 3mm [color="Red (633nm)" package="3 mm [THT]"]
  1l6 = LED - 3mm [color="Red (633nm)" package="3 mm [THT]"]
  dot1 = LED - 3mm [color="Red (633nm)" package="3 mm [THT]"]
  B11 = LED - 3mm [color="Red (633nm)" package="3 mm [THT]"]
  Brightness = Pushbutton [package="[THT]"]
  Rdot = Resistor [tolerance=±5% resistance=220 package=THT]

nets:
  N1: Ri.Pin_0, Arduino.D5
  N2: Ri.Pin_1, i1.anode, i2.anode, i3.anode
  N3: R1l.Pin_0, 1l2.anode, 1l4.anode, 1l3.anode, 1l1.anode, 1l5.anode, 1l6.anode
  N4: R1l.Pin_1, Arduino.D9
  N5: R2l.Pin_0, 2l3.anode, 2l4.anode, 2l5.anode, 2l6.anode, 2l2.anode, 2l1.anode
  N6: R2l.Pin_1, Arduino.D11
  N7: RB.Pin_0, Arduino.D3
  N8: RB.Pin_1, B1.anode, B4.anode, B3.anode, B7.anode, B8.anode, B9.anode, B10.anode, B5.anode, B6.anode, B2.anode, B11.anode
  GND: i1.cathode, i2.cathode, i3.cathode, 1l2.cathode, 1l4.cathode, 1l3.cathode, 2l3.cathode, 2l4.cathode, 2l5.cathode, 2l6.cathode, 1l1.cathode, B1.cathode, B4.cathode, B3.cathode, B7.cathode, B8.cathode, B9.cathode, B10.cathode, B5.cathode, B6.cathode, B2.cathode, Arduino.GND, Reset.Pin_1, Reset.Pin_2, Mode.Pin_1, Mode.Pin_2, 2l2.cathode, 2l1.cathode, 1l5.cathode, 1l6.cathode, dot1.cathode, B11.cathode, Brightness.Pin_1, Brightness.Pin_2
  N9: Arduino.D12, Brightness.Pin_3, Brightness.Pin_4
  N10: Arduino.D6, Rdot.Pin_0
  N11: Arduino.D4, Mode.Pin_3, Mode.Pin_4
  N12: Arduino.RST, Reset.Pin_3, Reset.Pin_4
  N13: dot1.anode, Rdot.Pin_1

notes:
  B
  i
  1l
  2l
  Reset
  Brightness
  Mode
  dot
