# Fritzing sketch Eric (saved by Fritzing 0.7.11b)
breadboards: 1
stripboards: 4

parts:
  Rr = Resistor [tolerance=±5% resistance=220 package=THT]
  Ri = Resistor [tolerance=±5% resistance=220 package=THT]
  Rc = Resistor [tolerance=±5% resistance=220 package=THT]
  RE = Resistor [tolerance=±5% resistance=220 package=THT]
  Rdot = Resistor [tolerance=±5% resistance=220 package=THT]
  r1 = LED - 3mm [color="Red (633nm)" package="3 mm [THT]"]
  r4 = LED - 3mm [color="Red (633nm)" package="3 mm [THT]"]
  r5 = LED - 3mm [color="Red (633nm)" package="3 mm [THT]"]
  r2 = LED - 3mm [color="Red (633nm)" package="3 mm [THT]"]
  r3 = LED - 3mm [color="Red (633nm)" package="3 mm [THT]"]
  i1 = LED - 3mm [color="Red (633nm)" package="3 mm [THT]"]
  i2 = LED - 3mm [color="Red (633nm)" package="3 mm [THT]"]
  i3 = LED - 3mm [color="Red (633nm)" package="3 mm [THT]"]
  c1 = LED - 3mm [color="Red (633nm)" package="3 mm [THT]"]
  c2 = LED - 3mm [color="Red (633nm)" package="3 mm [THT]"]
  c3 = LED - 3mm [color="Red (633nm)" package="3 mm [THT]"]
  c4 = LED - 3mm [color="Red (633nm)" package="3 mm [THT]"]
  c5 = LED - 3mm [color="Red (633nm)" package="3 mm [THT]"]
  c6 = LED - 3mm [color="Red (633nm)" package="3 mm [THT]"]
  dot1 = LED - 3mm [color="Red (633nm)" package="3 mm [THT]"]
  E1 = LED - 3mm [color="Red (633nm)" package="3 mm [THT]"]
  E4 = LED - 3mm [color="Red (633nm)" package="3 mm [THT]"]
  E3 = LED - 3mm [color="Red (633nm)" package="3 mm [THT]"]
  E7 = LED - 3mm [color="Red (633nm)" package="3 mm [THT]"]
  E8 = LED - 3mm [color="Red (633nm)" package="3 mm [THT]"]
  E9 = LED - 3mm [color="Red (633nm)" package="3 mm [THT]"]
  E10 = LED - 3mm [color="Red (633nm)" package="3 mm [THT]"]
  E5 = LED - 3mm [color="Red (633nm)" package="3 mm [THT]"]
  E6 = LED - 3mm [color="Red (633nm)" package="3 mm [THT]"]
  E2 = LED - 3mm [color="Red (633nm)" package="3 mm [THT]"]
  Arduino = Arduino
  Reset = Pushbutton [package="[THT]"]
  Mode = Pushbutton [package="[THT]"]
  Brightness = Pushbutton [package="[THT]"]
  QE = PNP-Transistor [package="TO92 [THT]"]
  Qc = PNP-Transistor [package="TO92 [THT]"]
  Qr = PNP-Transistor [package="TO92 [THT]"]
  Qi = PNP-Transistor [package="TO92 [THT]"]
  Qdot = PNP-Transistor [package="TO92 [THT]"]
  MC14490 = IC, DIP package, 16 pins [chip_label=MC14490]
  DC_Power1 = DC Power [voltage=5]
  DC_Power2 = DC Power [voltage=5]
  C1 = Electrolytic Capacitor [capacitance=1µF package="100 mil [THT, electrolytic]"]
  MIC = Microphone
  Q1 = NPN-Transistor [package="TO92 [THT]"]  # not connected

nets:
  N1: Rr.Pin_0, r1.anode, r4.anode, r5.anode, r2.anode, r3.anode
  N2: Rr.Pin_1, Qr.C
  N3: Ri.Pin_0, i1.anode, i2.anode, i3.anode
  N4: Ri.Pin_1, Qi.C
  N5: Rc.Pin_0, c1.anode, c2.anode, c3.anode, c4.anode, c5.anode, c6.anode
  N6: Rc.Pin_1, Qc.C
  N7: RE.Pin_0, QE.C
  N8: RE.Pin_1, E1.anode, E4.anode, E3.anode, E7.anode, E8.anode, E9.anode, E10.anode, E5.anode, E6.anode, E2.anode
  N9: Rdot.Pin_0, dot1.anode
  N10: Rdot.Pin_1, Qdot.C
  GND: r1.cathode, r4.cathode, r5.cathode, r2.cathode, r3.cathode, i1.cathode, i2.cathode, i3.cathode, c1.cathode, c2.cathode, c3.cathode, c4.cathode, c5.cathode, c6.cathode, dot1.cathode, E1.cathode, E4.cathode, E3.cathode, E7.cathode, E8.cathode, E9.cathode, E10.cathode, E5.cathode, E6.cathode, E2.cathode, Arduino.GND, Reset.Pin_1, Reset.Pin_2, Mode.Pin_1, Mode.Pin_2, Brightness.Pin_1, Brightness.Pin_2, MC14490.pin9, MC14490.pin12, C1.-, MIC.pin1
  N11: Arduino.D13, Mode.Pin_3, Mode.Pin_4, MC14490.pin14
  N12: Arduino.D12, Brightness.Pin_3, Brightness.Pin_4, MC14490.pin16
  N13: Arduino.D11, QE.B
  N14: Arduino.D10, Qr.B
  N15: Arduino.D9, Qi.B
  N16: Arduino.D6, Qdot.B
  N17: Arduino.D4, Qc.B
  N18: Arduino.D3, MC14490.pin4
  N19: Arduino.D2, MC14490.pin2
  N20: Arduino.RST, Reset.Pin_3, Reset.Pin_4
  N21: Arduino.+5V, QE.E, Qc.E, Qr.E, Qi.E, Qdot.E, MC14490.pin1, MC14490.pin3, MC14490.pin5, MC14490.pin7, DC_Power1.V+, DC_Power2.V+
  N22: MC14490.pin10, C1.+

notes:
  E
  r
  i
  dot
  c
  Reset
  Brightness
  Mode
