# Fritzing sketch Matt (saved by Fritzing 0.7.11b)
breadboards: 1
stripboards: 4

parts:
  Ra = Resistor [tolerance=±5% resistance=220 package=THT]
  R1t = Resistor [tolerance=±5% resistance=220 package=THT]
  R2t = Resistor [tolerance=±5% resistance=220 package=THT]
  RM = Resistor [tolerance=±5% resistance=220 package=THT]
  a1 = LED - 3mm [color="Red (633nm)" package="3 mm [THT]"]
  a5 = LED - 3mm [color="Red (633nm)" package="3 mm [THT]"]
  a8 = LED - 3mm [color="Red (633nm)" package="3 mm [THT]"]
  a2 = LED - 3mm [color="Red (633nm)" package="3 mm [THT]"]
  a3 = LED - 3mm [color="Red (633nm)" package="3 mm [THT]"]
  1t2 = LED - 3mm [color="Red (633nm)" package="3 mm [THT]"]
  1t4 = LED - 3mm [color="Red (633nm)" package="3 mm [THT]"]
  1t3 = LED - 3mm [color="Red (633nm)" package="3 mm [THT]"]
  2t3 = LED - 3mm [color="Red (633nm)" package="3 mm [THT]"]
  2t4 = LED - 3mm [color="Red (633nm)" package="3 mm [THT]"]
  2t5 = LED - 3mm [color="Red (633nm)" package="3 mm [THT]"]
  2t6 = LED - 3mm [color="Red (633nm)" package="3 mm [THT]"]
  2t7 = LED - 3mm [color="Red (633nm)" package="3 mm [THT]"]
  1t1 = LED - 3mm [color="Red (633nm)" package="3 mm [THT]"]
  M1 = LED - 3mm [color="Red (633nm)" package="3 mm [THT]"]
  M4 = LED - 3mm [color="Red (633nm)" package="3 mm [THT]"]
  M3 = LED - 3mm [color="Red (633nm)" package="3 mm [THT]"]
  M7 = LED - 3mm [color="Red (633nm)" package="3 mm [THT]"]
  M8 = LED - 3mm [color="Red (633nm)" package="3 mm [THT]"]
  M9 = LED - 3mm [color="Red (633nm)" package="3 mm [THT]"]
  M10 = LED - 3mm [color="Red (633nm)" package="3 mm [THT]"]
  M5 = LED - 3mm [color="Red (633nm)" package="3 mm [THT]"]
  M6 = LED - 3mm [color="Red (633nm)" package="3 mm [THT]"]
  M2 = LED - 3mm [color="Red (633nm)" package="3 mm [THT]"]
  Arduino = Arduino
  Reset = Pushbutton [package="[THT]"]
  Mode = Pushbutton [package="[THT]"]
  2t2 = LED - 3mm [color="Red (633nm)" package="3 mm [THT]"]
  2t1 = LED - 3mm [color="Red (633nm)" package="3 mm [THT]"]
  1t5 = LED - 3mm [color="Red (633nm)" package="3 mm [THT]"]
  1t6 = LED - 3mm [color="Red (633nm)" package="3 mm [THT]"]
  1t7 = LED - 3mm [color="Red (633nm)" package="3 mm [THT]"]
  a6 = LED - 3mm [color="Red (633nm)" package="3 mm [THT]"]
  a9 = LED - 3mm [color="Red (633nm)" package="3 mm [THT]"]
  a10 = LED - 3mm [color="Red (633nm)" package="3 mm [THT]"]
  a4 = LED - 3mm [color="Red (633nm)" package="3 mm [THT]"]
  a7 = LED - 3mm [color="Red (633nm)" package="3 mm [THT]"]
  M11 = LED - 3mm [color="Red (633nm)" package="3 mm [THT]"]
  M12 = LED - 3mm [color="Red (633nm)" package="3 mm [THT]"]
  M13 = LED - 3mm [color="Red (633nm)" package="3 mm [THT]"]
  Brightness = Pushbutton [package="[THT]"]

nets:
  N1: Ra.Pin_0, Arduino.D5
  N2: Ra.Pin_1, a1.anode, a5.anode, a8.anode, a2.anode, a3.anode, a6.anode, a9.anode, a10.anode, a4.anode, a7.anode
  N3: R1t.Pin_0, 1t2.anode, 1t4.anode, 1t3.anode, 1t1.anode, 1t5.anode, 1t6.anode, 1t7.anode
  N4: R1t.Pin_1, Arduino.D9
  N5: R2t.Pin_0, 2t3.anode, 2t4.anode, 2t5.anode, 2t6.anode, 2t7.anode, 2t2.anode, 2t1.anode
  N6: R2t.Pin_1, Arduino.D11
  N7: RM.Pin_0, Arduino.D3
  N8: RM.Pin_1, M1.anode, M4.anode, M3.anode, M7.anode, M8.anode, M9.anode, M10.anode, M5.anode, M6.anode, M2.anode, M11.anode, M12.anode, M13.anode
  GND: a1.cathode, a5.cathode, a8.cathode, a2.cathode, a3.cathode, 1t2.cathode, 1t4.cathode, 1t3.cathode, 2t3.cathode, 2t4.cathode, 2t5.cathode, 2t6.cathode, 2t7.cathode, 1t1.cathode, M1.cathode, M4.cathode, M3.cathode, M7.cathode, M8.cathode, M9.cathode, M10.cathode, M5.cathode, M6.cathode, M2.cathode, Arduino.GND, Reset.Pin_1, Reset.Pin_2, Mode.Pin_1, Mode.Pin_2, 2t2.cathode, 2t1.cathode, 1t5.cathode, 1t6.cathode, 1t7.cathode, a6.cathode, a9.cathode, a10.cathode, a4.cathode, a7.cathode, M11.cathode, M12.cathode, M13.cathode, Brightness.Pin_1, Brightness.Pin_2
  N9: Arduino.D12, Brightness.Pin_3, Brightness.Pin_4
  N10: Arduino.D4, Mode.Pin_3, Mode.Pin_4
  N11: Arduino.RST, Reset.Pin_3, Reset.Pin_4

notes:
  M
  a
  1t
  2t
  Reset
  Brightness
  Mode
