# Fritzing sketch RDI (saved by Fritzing 0.7.12b)
stripboards: 3
breadboards: 1

parts:
  RD = Resistor [tolerance=±5% resistance=220 package=THT]
  RI = Resistor [tolerance=±5% resistance=220 package=THT]
  RR = Resistor [tolerance=±5% resistance=220 package=THT]
  D5 = LED - 3mm [color="Red (633nm)" package="3 mm [THT]"]
  D6 = LED - 3mm [color="Red (633nm)" package="3 mm [THT]"]
  D4 = LED - 3mm [color="Red (633nm)" package="3 mm [THT]"]
  D3 = LED - 3mm [color="Red (633nm)" package="3 mm [THT]"]
  D1 = LED - 3mm [color="Red (633nm)" package="3 mm [THT]"]
  I5 = LED - 3mm [color="Red (633nm)" package="3 mm [THT]"]
  I6 = LED - 3mm [color="Red (633nm)" package="3 mm [THT]"]
  I8 = LED - 3mm [color="Red (633nm)" package="3 mm [THT]"]
  R1 = LED - 3mm [color="Red (633nm)" package="3 mm [THT]"]
  R3 = LED - 3mm [color="Red (633nm)" package="3 mm [THT]"]
  R4 = LED - 3mm [color="Red (633nm)" package="3 mm [THT]"]
  R7 = LED - 3mm [color="Red (633nm)" package="3 mm [THT]"]
  R9 = LED - 3mm [color="Red (633nm)" package="3 mm [THT]"]
  R8 = LED - 3mm [color="Red (633nm)" package="3 mm [THT]"]
  R10 = LED - 3mm [color="Red (633nm)" package="3 mm [THT]"]
  R5 = LED - 3mm [color="Red (633nm)" package="3 mm [THT]"]
  R6 = LED - 3mm [color="Red (633nm)" package="3 mm [THT]"]
  R2 = LED - 3mm [color="Red (633nm)" package="3 mm [THT]"]
  Arduino = Arduino
  Reset = Pushbutton [package="[THT]"]
  Mode = Pushbutton [package="[THT]"]
  DC_Power1 = DC Power [voltage=5]
  MIC = Microphone
  D2 = LED - 3mm [color="Red (633nm)" package="3 mm [THT]"]
  D10 = LED - 3mm [color="Red (633nm)" package="3 mm [THT]"]
  D7 = LED - 3mm [color="Red (633nm)" package="3 mm [THT]"]
  D9 = LED - 3mm [color="Red (633nm)" package="3 mm [THT]"]
  D8 = LED - 3mm [color="Red (633nm)" package="3 mm [THT]"]
  I7 = LED - 3mm [color="Red (633nm)" package="3 mm [THT]"]
  I4 = LED - 3mm [color="Red (633nm)" package="3 mm [THT]"]
  I3 = LED - 3mm [color="Red (633nm)" package="3 mm [THT]"]
  I2 = LED - 3mm [color="Red (633nm)" package="3 mm [THT]"]
  I1 = LED - 3mm [color="Red (633nm)" package="3 mm [THT]"]
  I9 = LED - 3mm [color="Red (633nm)" package="3 mm [THT]"]
  Brightness = Trimmer Potentiometer [maximum_resistance=10kΩ package=THT]
  Sensitivity = Trimmer Potentiometer [maximum_resistance=10kΩ package=THT]
  LM358 = LM 358 Dual Op-Amp [package="DIP8 [THT]"]
  C1 = Ceramic Capacitor [capacitance=100nF package="100 mil [THT, multilayer]"]
  Rp = Resistor [tolerance=±5% resistance=220 package="1206 [SMD]"]
  Ri = Resistor [tolerance=±5% resistance=220 package="1206 [SMD]"]
  Rb- = Resistor [tolerance=±5% resistance=220 package="1206 [SMD]"]
  Rb+ = Resistor [tolerance=±5% resistance=220 package="1206 [SMD]"]

nets:
  N1: RD.Pin_0, D5.anode, D6.anode, D4.anode, D3.anode, D1.anode, D2.anode, D10.anode, D7.anode, D9.anode, D8.anode
  N2: RD.Pin_1, Arduino.D10
  N3: RI.Pin_0, I5.anode, I6.anode, I8.anode, I7.anode, I4.anode, I3.anode, I2.anode, I1.anode, I9.anode
  N4: RI.Pin_1, Arduino.D9
  N5: RR.Pin_0, Arduino.D11
  N6: RR.Pin_1, R1.anode, R3.anode, R4.anode, R7.anode, R9.anode, R8.anode, R10.anode, R5.anode, R6.anode, R2.anode
  GND: D5.cathode, D6.cathode, D4.cathode, D3.cathode, D1.cathode, I5.cathode, I6.cathode, I8.cathode, R1.cathode, R3.cathode, R4.cathode, R7.cathode, R9.cathode, R8.cathode, R10.cathode, R5.cathode, R6.cathode, R2.cathode, Arduino.GND, Reset.Pin_1, Reset.Pin_2, Mode.Pin_1, Mode.Pin_2, DC_Power1.GND, MIC.pin1, D2.cathode, D10.cathode, D7.cathode, D9.cathode, D8.cathode, I7.cathode, I4.cathode, I3.cathode, I2.cathode, I1.cathode, I9.cathode, Brightness.leg2, LM358.connector3, Rb-.Pin_0
  N7: Arduino.D13, Mode.Pin_3, Mode.Pin_4
  N8: Arduino.RST, Reset.Pin_3, Reset.Pin_4
  N9: Arduino.+5V, DC_Power1.V+, Brightness.leg1, LM358.connector7, Rp.Pin_0, Rb+.Pin_1
  N10: Arduino.A0, Brightness.wiper
  N11: Arduino.A1, Sensitivity.wiper, Sensitivity.leg2, LM358.connector0
  N12: MIC.pin2, C1.0, Rp.Pin_1
  N13: Sensitivity.leg1, LM358.connector1, Ri.Pin_1
  N14: LM358.connector2, Rb-.Pin_1, Rb+.Pin_0
  N15: C1.1, Ri.Pin_0

notes:
  R
  D
  I
  Reset
  Brightness
  Mode
  RDI v1.1 By Eric Menze 7.4.2013
  Code and Schematic at github.com/Ehryk
